# Fritzing sketch led指示灯 (saved by Fritzing 0.9.3b)
circuit board: 4.56746cm x 3.75442cm
perfboards: 1

parts:
  R1 = Resistor [tolerance=±5% resistance=1k package=THT]
  Q1 = NPN-Transistor [part_number=8050 package="TO92 [THT]"]
  Q2 = NPN-Transistor [part_number=8050 package="TO92 [THT]"]
  Q3 = NPN-Transistor [part_number=8050 package="TO92 [THT]"]
  R2 = Resistor [tolerance=±5% resistance=1k package=THT]
  R3 = Resistor [tolerance=±5% resistance=1k package=THT]
  LED1 = LED - 5mm [color="Red (633nm)" package="5 mm [THT]"]
  LED2 = LED - 5mm [color="Green (570nm)" package="5 mm [THT]"]
  LED3 = LED - 5mm [color="Green (565nm)" package="5 mm [THT]"]
  U1 = SWITCH_SPDT [package=kps-1290]
  J1 = female pin header, 5 pins [form="♀ (female)"]
  R4 = Resistor [tolerance=±5% resistance=1k package=THT]
  R5 = Resistor [tolerance=±5% resistance=1k package=THT]
  R6 = Resistor [tolerance=±5% resistance=1k package=THT]

nets:
  N1: R1.Pin_0, Q1.C
  N2: R1.Pin_1, LED1.cathode
  GND: Q1.E, Q2.E, Q3.E, J1.pin2
  N3: Q1.B, R4.Pin_1
  N4: Q2.B, R5.Pin_0
  N5: Q2.C, R2.Pin_0
  N6: Q3.B, R6.Pin_0
  N7: Q3.C, R3.Pin_0
  N8: R2.Pin_1, LED2.cathode
  N9: R3.Pin_1, LED3.cathode
  N10: LED1.anode, LED2.anode, LED3.anode, U1.O
  5V: U1.P, J1.pin1
  N11: J1.pin3, R4.Pin_0
  N12: J1.pin4, R5.Pin_1
  N13: J1.pin5, R6.Pin_1
