# Fritzing sketch 蜂鸣器 (saved by Fritzing 0.9.3b)
circuit board: 5cm x 3.5cm
perfboards: 1

parts:
  D1 = Rectifier Diode [part_number=1N4001 package="300 mil [THT]"]
  Q1 = NPN-Transistor [package="TO92 [THT]"]
  SP1 = SPEAKER [package=pcb_mount_speaker]
  R1 = Resistor [tolerance=±5% resistance=1k package=THT]
  C1 = Ceramic Capacitor [capacitance=100nF package="100 mil [THT, multilayer]"]
  J1 = female pin header, 3 pins [form="♀ (female)"]
  LED1 = LED - 5mm [color="Red (633nm)" package="5 mm [THT]"]
  Q2 = NPN-Transistor [package="TO92 [THT]"]
  R2 = Resistor [tolerance=±5% resistance=1k package=THT]
  S1 = Round Pushbutton

nets:
  N1: D1.cathode, SP1.+, C1.1, S1.leg0
  N2: D1.anode, Q1.C, SP1.-
  GND: Q1.E, C1.0, J1.pin2, Q2.E
  N3: Q1.B, R1.Pin_1, Q2.B
  N4: R1.Pin_0, J1.pin3
  5V: J1.pin1, LED1.anode, S1.leg1
  N5: LED1.cathode, R2.Pin_0
  N6: Q2.C, R2.Pin_1
